# Fritzing sketch schema (saved by Fritzing 0.9.2b)
breadboards: 1

parts:
  U1 = ESP8266 WiFi Module [part_number=ESP8266]
  S4 = Magnetic Door Switch [package=reed_switch_plastic]
  S5 = Magnetic Door Switch [package=reed_switch_plastic]
  Composant1 = Arduino Uno (Rev3)
  R1 = Resistor [tolerance=±5% resistance=220 package=THT]
  R2 = Resistor [tolerance=±5% resistance=220 package=THT]
  U4 = 4-Channel 5v Relay Shield [package=relay-4ch5v10a]

nets:
  N1: U1.RXD, Composant1.D11_PWM/MOSI
  VCC: U1.VCC, U1.CH_PD, S4.2, S5.2, Composant1.3V3
  N2: U1.GPIO_0, S4.1, R1.Pin_1
  N3: U1.GPIO_2, S5.1, R2.Pin_1
  GND: U1.GND, Composant1.GND, U4.GND
  N4: U1.TXD, Composant1.D10_PWM/SS
  N5: Composant1.D2, U4.IN1
  N6: Composant1.D3_PWM, U4.IN2
  N7: Composant1.5V, U4.IN4

custom parts:
  ESP8266 WiFi Module: Generic WiFi Module based on the ESP8266 with onboard PCB antenna and UART communications
  4-Channel 5v Relay Shield: 4 Channel 5v Relay Shield w. 2x SPD-06VDC-SD-C
