# Fritzing sketch schema2 (saved by Fritzing 0.9.2b)
breadboards: 1

parts:
  S4 = Magnetic Door Switch [package=reed_switch_plastic]
  S5 = Magnetic Door Switch [package=reed_switch_plastic]
  R1 = Resistor [tolerance=±5% resistance=220 package=THT]
  R2 = Resistor [tolerance=±5% resistance=220 package=THT]
  U4 = 4-Channel 5v Relay Shield [package=relay-4ch5v10a]
  U5 = Breadboard Power Supply [package=THT]
  U6 = NodeMCU V3.0

nets:
  N1: S4.1, R1.Pin_1, U6.D8
  N2: S4.2, S5.2
  N3: S5.1, R2.Pin_1, U6.D6
  N4: U4.IN1, U6.D7
  N5: U5.pin1, U5.pin2
  N6: U5.pin3, U5.pin4
  N7: U5.pin5, U5.pin6, U6.GND
  N8: U5.pin7, U5.pin8, U6.3V3

custom parts:
  4-Channel 5v Relay Shield: 4 Channel 5v Relay Shield w. 2x SPD-06VDC-SD-C
  Breadboard Power Supply: Représentation Carte Breadboard Power Supply
  NodeMCU V3.0: ESP8266 based NodeMCU
