# Fritzing sketch schema3 (saved by Fritzing 0.9.2b)
breadboards: 1

parts:
  S4 = Magnetic Door Switch [package=reed_switch_plastic]
  R2 = Resistor [tolerance=±5% resistance=220 package=THT]
  U4 = 4-Channel 5v Relay Shield [package=relay-4ch5v10a]
  Composant2 = Arduino Ethernet Shield (Rev3)

nets:
  N1: S4.1, R2.Pin_1, Composant2.D7
  N2: S4.2, Composant2.5V
  N3: R2.Pin_0, Composant2.GND
  N4: U4.IN1, Composant2.D2

custom parts:
  4-Channel 5v Relay Shield: 4 Channel 5v Relay Shield w. 2x SPD-06VDC-SD-C
